// Logisim project cpu.circ as structural Verilog: 4 circuits, main circuit CPU
module CPU (
  output [47:0] cpu_out,
  output halt
);

  wire and_1_out, and_2_out, clk_out, decoder_1_out0, decoder_1_out1, decoder_1_out2, decoder_1_out3,
       decoder_1_out4, decoder_2_out2, decoder_2_out3, not_1_out, not_2_out, or_1_out, or_2_out, reset_out;
  wire [2:0] adder_1_out, control_q, multiplexer_1_out, multiplexer_2_out;
  wire [15:0] adder_2_out, alu_1_c, bit_extender_1_out, InsMem_data, multiplexer_3_out, multiplexer_4_out,
       multiplexer_5_out, RA_q, ram_1_dout, RB_q, registerfile_1_a, registerfile_1_b, RM_q, RY_q;

  Clock clk (.out(clk_out));
  Button reset (.out(reset_out));
  Decoder #(.enable("false"), .select(3)) decoder_1 (
    .out0(decoder_1_out0), .out1(decoder_1_out1), .out2(decoder_1_out2), .out3(decoder_1_out3),
    .out4(decoder_1_out4), .sel(control_q));  // open: out5, out6, out7
  Multiplexer #(.width(3)) multiplexer_1 (
    .in0(cpu_out[18:16]), .in1(cpu_out[25:23]), .out(multiplexer_1_out), .sel(decoder_2_out3));
  and and_1 (and_1_out, not_1_out, decoder_1_out4);
  not not_1 (not_1_out, decoder_2_out3);
  Adder #(.width(3)) adder_1 (.a(control_q), .b(3'b001), .out(adder_1_out));  // open: cin, cout
  Register #(.width(3)) control (.D(multiplexer_2_out), .en(1'b1), .clk(not_2_out), .Q(control_q), .clr(reset_out));
  Multiplexer #(.width(3)) multiplexer_2 (
    .in0(adder_1_out), .in1(3'b000), .out(multiplexer_2_out), .sel(decoder_1_out4));
  not not_2 (not_2_out, clk_out);
  Register #(.width(16)) PC (.D(adder_2_out), .en(decoder_1_out0), .clk(clk_out), .Q(cpu_out[47:32]), .clr(reset_out));
  RegisterFile registerfile_1 (
    .Addr_A(cpu_out[22:20]), .Addr_B(multiplexer_1_out), .we(and_1_out), .Addr_C(cpu_out[25:23]),
    .clk(clk_out), .reset(reset_out), .C(RY_q), .A(registerfile_1_a), .B(registerfile_1_b));
  Adder #(.width(16)) adder_2 (.a(cpu_out[47:32]), .b(16'h1), .out(adder_2_out));  // open: cin, cout
  Register #(.width(16)) RA (.D(registerfile_1_a), .en(decoder_1_out1), .clk(clk_out), .Q(RA_q), .clr(reset_out));
  Register #(.width(16)) RB (.D(registerfile_1_b), .en(decoder_1_out1), .clk(clk_out), .Q(RB_q), .clr(reset_out));
  // Probe on cpu_out[19:16]
  ROM #(.addrWidth(16), .dataWidth(16)) InsMem (.addr(cpu_out[47:32]), .data(InsMem_data));
  Multiplexer #(.width(16)) multiplexer_3 (
    .in0(RB_q), .in1(bit_extender_1_out), .out(multiplexer_3_out), .sel(or_1_out));
  or or_1 (or_1_out, cpu_out[26], decoder_2_out3);
  assign bit_extender_1_out = {{12{cpu_out[19]}}, cpu_out[19:16]};  // Bit_Extender bit_extender_1
  ALU alu_1 (
    .A(RA_q), .fun(cpu_out[29:27]), .B(multiplexer_3_out), .C(alu_1_c));  // open: carry, zero, negative, overflow
  // Probe on cpu_out[31:16]
  Register #(.width(16)) RZ (.D(alu_1_c), .en(decoder_1_out2), .clk(clk_out), .Q(cpu_out[15:0]), .clr(reset_out));
  Register #(.width(16)) RM (.D(RB_q), .en(decoder_1_out2), .clk(clk_out), .Q(RM_q), .clr(reset_out));
  Register #(.width(16)) IR (.D(InsMem_data), .en(decoder_1_out0), .clk(clk_out), .Q(cpu_out[31:16]), .clr(reset_out));
  Multiplexer #(.select(2), .width(16)) multiplexer_4 (
    .in0(cpu_out[15:0]), .in2(ram_1_dout), .in3(cpu_out[15:0]), .out(multiplexer_4_out), .sel(cpu_out[31:30]));  // open: in1
  // Probe on cpu_out[26]
  // Probe on cpu_out[29:27]
  Decoder #(.enable("false"), .select(2)) decoder_2 (
    .out2(decoder_2_out2), .out3(decoder_2_out3), .sel(cpu_out[31:30]));  // open: out0, out1
  Register #(.width(16)) RY (.D(multiplexer_4_out), .en(decoder_1_out3), .clk(clk_out), .Q(RY_q), .clr(reset_out));
  // Probe on cpu_out[19:16]
  // Probe on cpu_out[25:23]
  Comparator #(.width(16)) comparator_1 (.a(cpu_out[31:16]), .b(16'h4380), .eq(halt));  // open: gt, lt
  // Probe on cpu_out[22:20]
  Multiplexer #(.width(16)) multiplexer_5 (
    .in0({16{1'b0}}), .in1(cpu_out[15:0]), .out(multiplexer_5_out), .sel(or_2_out));
  or or_2 (or_2_out, decoder_2_out2, decoder_2_out3);
  and and_2 (and_2_out, decoder_1_out3, decoder_2_out3);
  RAM #(.addrWidth(16), .dataWidth(16), .enables("line")) ram_1 (
    .addr(multiplexer_5_out), .we(and_2_out), .clk(clk_out), .din(RM_q), .dout(ram_1_dout));

  // Notes on the sheet:
  //   contents of InsMem (hex, n*v repeats v):
  //   490 522 5b4 c4a0 c5a0 f21 7f3 c4e0 c7e0 646 c4b0 c630 f31 c4e0 c7e0 6d7 6d1 c4c0 c6c0 f41 c4e0 c7e0
  //   8720 760 ca1 8510 520 1400 2 87e0 7f0 ce1 8510 520 2 85f0 5b0 cf1 8510 520 2 4380
endmodule

module ALU (
  input  [2:0] fun,
  input  [15:0] A,
  input  [15:0] B,
  output carry,
  output [15:0] C,
  output zero,
  output negative,
  output overflow
);

  wire and_2_out, and_3_out, not_2_out, not_3_out, not_4_out;
  wire [15:0] adder_1_out, and_1_out, multiplexer_1_out, negator_1_out, not_1_out, or_1_out, shifter_1_out,
       shifter_2_out, shifter_3_out;

  Negator #(.width(16)) negator_1 (.in(B), .out(negator_1_out));
  assign and_1_out = A & B;  // AND_Gate and_1, 16 bits wide
  assign or_1_out = A | B;  // OR_Gate or_1, 16 bits wide
  Shifter #(.width(16)) shifter_1 (.in(A), .\dist (B[3:0]), .out(shifter_1_out));
  Shifter #(.shift("lr"), .width(16)) shifter_2 (.in(A), .\dist (B[3:0]), .out(shifter_2_out));
  Shifter #(.shift("ar"), .width(16)) shifter_3 (.in(A), .\dist (B[3:0]), .out(shifter_3_out));
  Multiplexer #(.width(16)) multiplexer_1 (.in0(B), .in1(negator_1_out), .out(multiplexer_1_out), .sel(fun[0]));
  Adder #(.width(16)) adder_1 (.a(A), .b(multiplexer_1_out), .out(adder_1_out), .cin(1'b0), .cout(carry));
  assign not_1_out = ~or_1_out;  // NOT_Gate not_1, 16 bits wide
  not not_2 (not_2_out, multiplexer_1_out[15]);
  not not_3 (not_3_out, A[15]);
  not not_4 (not_4_out, adder_1_out[15]);
  Multiplexer #(.select(3), .width(16)) multiplexer_2 (
    .in0(adder_1_out), .in1(adder_1_out), .in2(and_1_out), .in3(or_1_out), .in4(not_1_out),
    .in5(shifter_1_out), .in6(shifter_2_out), .in7(shifter_3_out), .out(C), .sel(fun));
  and and_2 (and_2_out, not_2_out, not_3_out, adder_1_out[15]);
  and and_3 (and_3_out, A[15], multiplexer_1_out[15], not_4_out);
  or or_2 (overflow, and_2_out, and_3_out);
  Comparator #(.width(16)) comparator_1 (.a(C), .b({16{1'b0}}), .eq(zero), .lt(negative));  // open: gt
endmodule

module RegisterFile (
  input  [2:0] Addr_A,
  input  [2:0] Addr_B,
  input  we,
  input  [2:0] Addr_C,
  input  clk,
  input  reset,
  input  [15:0] C,
  output [15:0] A,
  output [15:0] B
);

  wire and_1_out, and_2_out, and_3_out, and_4_out, and_5_out, and_6_out, and_7_out, and_8_out,
       decoder_1_out0, decoder_1_out1, decoder_1_out2, decoder_1_out3, decoder_1_out4, decoder_1_out5,
       decoder_1_out6, decoder_1_out7;
  wire [15:0] R0_q, R1_q, R2_q, R3_q, R4_q, R5_q, R6_q, R7_q;

  Decoder #(.enable("false"), .select(3)) decoder_1 (
    .out0(decoder_1_out0), .out1(decoder_1_out1), .out2(decoder_1_out2), .out3(decoder_1_out3),
    .out4(decoder_1_out4), .out5(decoder_1_out5), .out6(decoder_1_out6), .out7(decoder_1_out7), .sel(Addr_C));
  and and_1 (and_1_out, decoder_1_out0, we);
  and and_2 (and_2_out, decoder_1_out1, we);
  and and_3 (and_3_out, decoder_1_out2, we);
  and and_4 (and_4_out, decoder_1_out3, we);
  and and_5 (and_5_out, decoder_1_out4, we);
  and and_6 (and_6_out, decoder_1_out5, we);
  and and_7 (and_7_out, decoder_1_out6, we);
  and and_8 (and_8_out, decoder_1_out7, we);
  Register #(.width(16)) R0 (.D(C), .en(and_1_out), .clk(clk), .Q(R0_q), .clr(reset));
  Register #(.width(16)) R1 (.D(C), .en(and_2_out), .clk(clk), .Q(R1_q), .clr(reset));
  Register #(.width(16)) R2 (.D(C), .en(and_3_out), .clk(clk), .Q(R2_q), .clr(reset));
  Register #(.width(16)) R3 (.D(C), .en(and_4_out), .clk(clk), .Q(R3_q), .clr(reset));
  Register #(.width(16)) R4 (.D(C), .en(and_5_out), .clk(clk), .Q(R4_q), .clr(reset));
  Register #(.width(16)) R5 (.D(C), .en(and_6_out), .clk(clk), .Q(R5_q), .clr(reset));
  Register #(.width(16)) R6 (.D(C), .en(and_7_out), .clk(clk), .Q(R6_q), .clr(reset));
  Register #(.width(16)) R7 (.D(C), .en(and_8_out), .clk(clk), .Q(R7_q), .clr(reset));
  Multiplexer #(.select(3), .width(16)) multiplexer_1 (
    .in0(R0_q), .in1(R1_q), .in2(R2_q), .in3(R3_q), .in4(R4_q), .in5(R5_q), .in6(R6_q), .in7(R7_q), .out(A),
    .sel(Addr_A));
  Multiplexer #(.select(3), .width(16)) multiplexer_2 (
    .in0(R0_q), .in1(R1_q), .in2(R2_q), .in3(R3_q), .in4(R4_q), .in5(R5_q), .in6(R6_q), .in7(R7_q), .out(B),
    .sel(Addr_B));
endmodule

module RegisterFileTester (
  output halt,
  output [15:0] A,
  output [15:0] B,
  output clk
);

  wire undriven;
  wire [2:0] Addr_A_data, Addr_B_data, Addr_C_data;
  wire [3:0] adder_1_out, addr_q;
  wire [15:0] C_data;

  Clock clock_1 (.out(clk));
  ROM #(.addrWidth(4), .dataWidth(3)) Addr_A (.addr(addr_q), .data(Addr_A_data));
  ROM #(.addrWidth(4), .dataWidth(3)) Addr_B (.addr(addr_q), .data(Addr_B_data));
  ROM #(.addrWidth(4), .dataWidth(3)) Addr_C (.addr(addr_q), .data(Addr_C_data));
  ROM #(.addrWidth(4), .dataWidth(1)) we (.addr(addr_q));  // open: data
  ROM #(.addrWidth(4), .dataWidth(16)) C (.addr(addr_q), .data(C_data));
  Adder #(.width(4)) adder_1 (.a(addr_q), .b(4'b0001), .out(adder_1_out), .cin(1'b0));  // open: cout
  Register #(.width(4)) addr (.D(adder_1_out), .en(1'b1), .clk(clk), .Q(addr_q), .clr(1'b0));
  Comparator #(.width(4)) comparator_1 (.a(addr_q), .b(4'b1111), .eq(halt));  // open: gt, lt
  RegisterFile registerfile_1 (
    .Addr_A(Addr_A_data), .Addr_B(Addr_B_data), .we(undriven), .Addr_C(Addr_C_data), .clk(clk), .reset(1'b0),
    .C(C_data), .A(A), .B(B));

  // Notes on the sheet:
  //   contents of Addr_A (hex, n*v repeats v):
  //   5 2 7 3 2 0 2 6 2 4 1 3 5 5 2 6
  //   contents of Addr_B (hex, n*v repeats v):
  //   4 4 6 0 2 3 5 5 5 0 0 4 5 3 7 5
  //   contents of Addr_C (hex, n*v repeats v):
  //   0 5 0 5 5 7 2 3 6 4 0 4 7 7 4 6
  //   contents of we (hex, n*v repeats v):
  //   0 0 0 1 0 0 1 0 0 0 1 1 0 0 1 1
  //   contents of C (hex, n*v repeats v):
  //   1 4 c f 0 5 9 7 c b 9 f b 9 1 e
endmodule
